# Fritzing sketch electronic_design (saved by Fritzing 0.9.2b)
breadboards: 1

parts:
  RF1 = nRF8001 Bluetooth LE Breakout
  ARDUINO1 = Arduino Micro
  FSR1 = Basic Force Sensing Resistor (FSR) [package=THT]
  FSR2 = Basic Force Sensing Resistor (FSR) [package=THT]
  FSR3 = Basic Force Sensing Resistor (FSR) [package=THT]
  FSR4 = Basic Force Sensing Resistor (FSR) [package=THT]
  FSR5 = Basic Force Sensing Resistor (FSR) [package=THT]
  FSR6 = Basic Force Sensing Resistor (FSR) [package=THT]
  R1 = Resistor [tolerance=±5% resistance=1k package="0402 [SMD]"]
  R2 = Resistor [tolerance=±5% resistance=1k package="0402 [SMD]"]
  R3 = Resistor [tolerance=±5% resistance=1k package="0402 [SMD]"]
  R4 = Resistor [tolerance=±5% resistance=1k package="0402 [SMD]"]
  R5 = Resistor [tolerance=±5% resistance=1k package="0402 [SMD]"]
  R6 = Resistor [tolerance=±5% resistance=1k package="0402 [SMD]"]
  R7 = Resistor [tolerance=±5% resistance=1k package="0402 [SMD]"]
  FSR0 = Basic Force Sensing Resistor (FSR) [package=THT]

nets:
  N1: RF1.SCK, ARDUINO1.SCK
  N2: RF1.MISO, ARDUINO1.MOSI
  N3: RF1.MOSI, ARDUINO1.MISO
  N4: RF1.REQ, ARDUINO1.D10
  N5: RF1.RDY, ARDUINO1.D2
  N6: RF1.RST, ARDUINO1.D9
  N7: RF1.GND, ARDUINO1.GND#31
  VIN: RF1.VIN, ARDUINO1.5V, FSR2.pin_0, FSR3.pin_0, FSR4.pin_0, FSR5.pin_0, FSR6.pin_0, FSR0.pin_0
  N8: ARDUINO1.GND#6, R1.Pin_1, R2.Pin_1, R3.Pin_1, R4.Pin_1, R5.Pin_1, R6.Pin_1, R7.Pin_1
  N9: ARDUINO1.D4, R3.Pin_0, FSR0.pin_1
  N10: ARDUINO1.A0, FSR1.pin_1, R2.Pin_0
  N11: ARDUINO1.A1, FSR6.pin_1, R5.Pin_0
  N12: ARDUINO1.A2, FSR2.pin_1, R4.Pin_0
  N13: ARDUINO1.A3, FSR3.pin_1, R6.Pin_0
  N14: ARDUINO1.A4, FSR5.pin_1, R7.Pin_0
  N15: ARDUINO1.A5, FSR4.pin_1, R1.Pin_0

custom parts:
  nRF8001 Bluetooth LE Breakout: nRF8001 Breakout Board
  Arduino Micro: Arduino Micro Microcontroller
